// Logisim project project.circ as structural Verilog
module PC (
  input  [31:0] imm_b,
  input  [31:0] imm_j,
  input  [31:0] rs1_val,
  input  clk,
  input  [31:0] imm_i,
  input  reset,
  input  branch_taken,
  input  jump,
  input  jalr,
  output [31:0] pc_out,
  output [31:0] pc_plus_4,
  output [31:0] pc_next
);

  wire [31:0] adder_1_out, adder_3_out, adder_4_out, and_1_out, multiplexer_1_out, multiplexer_2_out;

  Register #(.width(32)) pc_reg (.D(pc_next), .en(1'b1), .clk(clk), .Q(pc_out), .clr(reset));
  Adder #(.width(32)) adder_1 (.a(rs1_val), .b(imm_i), .out(adder_1_out));  // open: cin, cout
  Adder #(.width(32)) adder_2 (.a(pc_out), .b(32'h4), .out(pc_plus_4));  // open: cin, cout
  Adder #(.width(32)) adder_3 (.a(pc_out), .b(imm_b), .out(adder_3_out));  // open: cin, cout
  Adder #(.width(32)) adder_4 (.a(pc_out), .b(imm_j), .out(adder_4_out));  // open: cin, cout
  assign and_1_out = adder_1_out & 32'hfffffffe;  // AND_Gate and_1, 32 bits wide
  Multiplexer #(.width(32)) multiplexer_1 (
    .in0(pc_plus_4), .in1(adder_3_out), .out(multiplexer_1_out), .sel(branch_taken));
  Multiplexer #(.width(32)) multiplexer_2 (
    .in0(multiplexer_1_out), .in1(adder_4_out), .out(multiplexer_2_out), .sel(jump));
  Multiplexer #(.width(32)) multiplexer_3 (.in0(multiplexer_2_out), .in1(and_1_out), .out(pc_next), .sel(jalr));
endmodule

module imem (
);

  ROM rom_1 ();  // open: addr, data
endmodule

module ImmGen (
  input  [31:0] instr,
  input  [2:0] imm_sel,
  output [31:0] imm_out
);

  wire [31:0] bit_extender_1_out, bit_extender_2_out, bit_extender_3_out, bit_extender_4_out;

  assign bit_extender_1_out = {{20{instr[7]}}, {instr[7], instr[11:8], instr[31:25]}};  // Bit_Extender bit_extender_1
  assign bit_extender_2_out = {{20{instr[31]}}, instr[31:20]};  // Bit_Extender bit_extender_2
  assign bit_extender_3_out = {{19{instr[31]}}, {instr[31], instr[7], instr[30:25], instr[11:8], 1'b0}};  // Bit_Extender bit_extender_3
  assign bit_extender_4_out = {{11{instr[31]}}, {instr[31], instr[19:12], instr[20], instr[30:21], 1'b0}};  // Bit_Extender bit_extender_4
  Multiplexer #(.select(3), .width(32)) multiplexer_1 (
    .in0(bit_extender_2_out), .in1(bit_extender_1_out), .in2(bit_extender_3_out),
    .in3({instr[31:12], {12{1'b0}}}), .in4(bit_extender_4_out), .out(imm_out), .sel(imm_sel));  // open: in5, in6, in7

  // Other names for the same wires on the sheet: p11_8[3:0] = instr[11:8]; p7 = instr[7]; p30_21[9:0] = instr[30:21];
  //   p31_12[19:0] = instr[31:12]; p30_25[5:0] = instr[30:25]; p20 = instr[20]; p19_12[7:0] = instr[19:12];
  //   p31 = instr[31]; p0 = instr[0]

  // Notes on the sheet:
  //   type-s
  //   type-i
  //   type-B
  //   type-u
  //   type-j
endmodule

module RegFile (
  input  [31:0] in_1,
  output [31:0] out_2
);

  wire clock_1_out;

  Clock clock_1 (.out(clock_1_out));
  Register #(.width(32)) register_1 (.D(in_1), .en(1'b1), .clk(clock_1_out), .Q(out_2), .clr(1'b1));
  Register #(.width(32)) register_2 ();  // open: D, en, clk, Q, clr
  Register #(.width(32)) register_3 ();  // open: D, en, clk, Q, clr
  Register #(.width(32)) register_4 ();  // open: D, en, clk, Q, clr
  Register #(.width(32)) register_5 ();  // open: D, en, clk, Q, clr
  Register #(.width(32)) register_6 ();  // open: D, en, clk, Q, clr
  Register #(.width(32)) register_7 ();  // open: D, en, clk, Q, clr
  Register #(.width(32)) register_8 ();  // open: D, en, clk, Q, clr
  Register #(.width(32)) register_9 ();  // open: D, en, clk, Q, clr
  Register #(.width(32)) register_10 ();  // open: D, en, clk, Q, clr
  Register #(.width(32)) register_11 ();  // open: D, en, clk, Q, clr
  Register #(.width(32)) register_12 ();  // open: D, en, clk, Q, clr
  Register #(.width(32)) register_13 ();  // open: D, en, clk, Q, clr
  Register #(.width(32)) register_14 ();  // open: D, en, clk, Q, clr
  Register #(.width(32)) register_15 ();  // open: D, en, clk, Q, clr
  Register #(.width(32)) register_16 ();  // open: D, en, clk, Q, clr
  Register #(.width(32)) register_17 ();  // open: D, en, clk, Q, clr
  Register #(.width(32)) register_18 ();  // open: D, en, clk, Q, clr
  Register #(.width(32)) register_19 ();  // open: D, en, clk, Q, clr
  Register #(.width(32)) register_20 ();  // open: D, en, clk, Q, clr
  Register #(.width(32)) register_21 ();  // open: D, en, clk, Q, clr
  Register #(.width(32)) register_22 ();  // open: D, en, clk, Q, clr
  Register #(.width(32)) register_23 ();  // open: D, en, clk, Q, clr
  Register #(.width(32)) register_24 ();  // open: D, en, clk, Q, clr
  Register #(.width(32)) register_25 ();  // open: D, en, clk, Q, clr
  Register #(.width(32)) register_26 ();  // open: D, en, clk, Q, clr
  Register #(.width(32)) register_27 ();  // open: D, en, clk, Q, clr
  Register #(.width(32)) register_28 ();  // open: D, en, clk, Q, clr
  Register #(.width(32)) register_29 ();  // open: D, en, clk, Q, clr
  Register #(.width(32)) register_30 ();  // open: D, en, clk, Q, clr
  Register #(.width(32)) register_31 ();  // open: D, en, clk, Q, clr
  Register #(.width(32)) register_32 ();  // open: D, en, clk, Q, clr
endmodule
